// Logisim project 000_NotGate.circ as structural Verilog: 1 circuit, main circuit main
module main (
  input  in_1,
  input  in_2,
  output out_3,
  output out_4
);

  wire transistor_1_out;

  Transistor transistor_1 (.in(1'b1), .out(transistor_1_out), .gate(1'b0));
  Transistor #(.\type ("n")) transistor_2 (.in(1'b0), .out(transistor_1_out), .gate(1'b0));
  not not_1 (out_3, in_1);
  // Probe on transistor_1_out
  nand nand_1 (out_4, in_2, in_2);
endmodule
