// Logisim project 001_NorGate.circ as structural Verilog: 1 circuit, main circuit main
module main (
);

  wire transistor_1_out, transistor_2_out;

  Transistor transistor_1 (.in(1'b1), .out(transistor_1_out), .gate(1'b0));
  Transistor transistor_2 (.in(transistor_1_out), .out(transistor_2_out), .gate(1'b0));
  Transistor #(.\type ("n")) transistor_3 (.in(1'b0), .out(transistor_2_out), .gate(1'b0));
  Transistor #(.\type ("n")) transistor_4 (.in(1'b0), .out(transistor_2_out), .gate(1'b0));
  // Probe on transistor_2_out
endmodule
