// Logisim project 002_NANDGate.circ as structural Verilog: 1 circuit, main circuit main
module main (
);

  wire transistor_1_out, transistor_4_out;

  Transistor transistor_1 (.in(1'b1), .out(transistor_1_out), .gate(1'b1));
  Transistor transistor_2 (.in(1'b1), .out(transistor_1_out), .gate(1'b0));
  Transistor #(.\type ("n")) transistor_3 (.in(transistor_4_out), .out(transistor_1_out), .gate(1'b0));
  Transistor #(.\type ("n")) transistor_4 (.in(1'b0), .out(transistor_4_out), .gate(1'b1));
  // Probe on transistor_1_out
endmodule
