// Logisim project 003_NANDBasedNotGate.circ as structural Verilog: 1 circuit, main circuit main
module main (
);

  wire transistor_1_out, transistor_3_out, transistor_6_out;

  Transistor transistor_1 (.in(1'b1), .out(transistor_1_out), .gate(1'b0));
  Transistor #(.\type ("n")) transistor_2 (.in(1'b0), .out(transistor_1_out), .gate(1'b0));
  Transistor transistor_3 (.in(1'b1), .out(transistor_3_out), .gate(1'b0));
  // Probe on transistor_1_out
  Transistor transistor_4 (.in(1'b1), .out(transistor_3_out), .gate(1'b0));
  Transistor #(.\type ("n")) transistor_5 (.in(transistor_6_out), .out(transistor_3_out), .gate(1'b0));
  Transistor #(.\type ("n")) transistor_6 (.in(1'b0), .out(transistor_6_out), .gate(1'b0));
  // Probe on transistor_3_out
endmodule
