// Logisim project 006_PQRLayout.circ as structural Verilog: 1 circuit, main circuit main
module main (
);

  wire transistor_1_out, transistor_3_out, transistor_5_out, transistor_8_out, transistor_9_out,
       transistor_11_out, transistor_13_out, transistor_16_out;

  Transistor transistor_1 (.in(1'b1), .out(transistor_1_out), .gate(1'b1));
  Transistor #(.\type ("n")) transistor_2 (.in(1'b0), .out(transistor_1_out), .gate(1'b1));
  Transistor transistor_3 (.in(1'b1), .out(transistor_3_out), .gate(1'b0));
  Transistor #(.\type ("n")) transistor_4 (.in(1'b0), .out(transistor_3_out), .gate(1'b0));
  Transistor transistor_5 (.in(1'b1), .out(transistor_5_out), .gate(transistor_1_out));
  Transistor transistor_6 (.in(1'b1), .out(transistor_5_out), .gate(transistor_3_out));
  Transistor #(.\type ("n")) transistor_7 (.in(transistor_8_out), .out(transistor_5_out), .gate(transistor_3_out));
  Transistor #(.\type ("n")) transistor_8 (.in(1'b0), .out(transistor_8_out), .gate(transistor_1_out));
  Transistor transistor_9 (.in(1'b1), .out(transistor_9_out), .gate(transistor_1_out));
  Transistor #(.\type ("n")) transistor_10 (.in(transistor_11_out), .out(transistor_9_out), .gate(transistor_1_out));
  Transistor #(.\type ("n")) transistor_11 (.in(1'b0), .out(transistor_11_out), .gate(1'b0));
  Transistor transistor_12 (.in(1'b1), .out(transistor_9_out), .gate(1'b0));
  Transistor transistor_13 (.in(1'b1), .out(transistor_13_out), .gate(transistor_3_out));
  Transistor transistor_14 (.in(1'b1), .out(transistor_13_out), .gate(transistor_9_out));
  // Probe on transistor_5_out
  // Probe on transistor_13_out
  Transistor #(.\type ("n")) transistor_15 (.in(transistor_16_out), .out(transistor_13_out), .gate(transistor_3_out));
  Transistor #(.\type ("n")) transistor_16 (.in(1'b0), .out(transistor_16_out), .gate(transistor_9_out));
endmodule
