// Logisim project 007_AndOtherImplementation.circ as structural Verilog: 1 circuit, main circuit main
module main (
);

  wire pull_resistor_2_node, pull_resistor_4_node, transistor_1_out, transistor_2_out, transistor_3_out,
       transistor_5_out, transistor_6_out, transistor_8_out, transistor_13_out, transistor_16_out,
       transistor_17_out, transistor_19_out, transistor_20_out;

  Transistor #(.\type ("n")) transistor_1 (.in(1'b1), .out(transistor_1_out), .gate(1'b1));
  Transistor #(.\type ("n")) transistor_2 (.in(transistor_1_out), .out(transistor_2_out), .gate(1'b1));
  Transistor transistor_3 (.in(1'b1), .out(transistor_3_out), .gate(1'b0));
  Transistor #(.\type ("n")) transistor_4 (.in(transistor_5_out), .out(transistor_3_out), .gate(1'b0));
  Transistor #(.\type ("n")) transistor_5 (.in(1'b0), .out(transistor_5_out), .gate(1'b0));
  Transistor transistor_6 (.in(1'b1), .out(transistor_6_out), .gate(1'b1));
  Transistor #(.\type ("n")) transistor_7 (.in(transistor_8_out), .out(transistor_6_out), .gate(1'b1));
  Transistor #(.\type ("n")) transistor_8 (.in(1'b0), .out(transistor_8_out), .gate(1'b1));
  Transistor transistor_9 (.in(1'b0), .out(transistor_2_out), .gate(1'b1));
  Transistor transistor_10 (.in(1'b1), .out(transistor_3_out), .gate(1'b0));
  Transistor transistor_11 (.in(1'b1), .out(transistor_6_out), .gate(1'b1));
  Transistor transistor_12 (.in(1'b0), .out(transistor_2_out), .gate(1'b1));
  Transistor transistor_13 (.in(1'b1), .out(transistor_13_out), .gate(transistor_3_out));
  Transistor transistor_14 (.in(1'b1), .out(transistor_13_out), .gate(transistor_3_out));
  Transistor #(.\type ("n")) transistor_15 (.in(transistor_16_out), .out(transistor_13_out), .gate(transistor_3_out));
  Transistor #(.\type ("n")) transistor_16 (.in(1'b0), .out(transistor_16_out), .gate(transistor_3_out));
  Transistor transistor_17 (.in(1'b1), .out(transistor_17_out), .gate(transistor_6_out));
  // Probe on transistor_17_out
  Transistor #(.\type ("n")) transistor_18 (.in(1'b0), .out(transistor_17_out), .gate(transistor_6_out));
  // Probe on transistor_13_out
  // Probe on transistor_2_out
  Transistor transistor_19 (.in(pull_resistor_2_node), .out(transistor_19_out), .gate(1'b1));
  Transistor transistor_20 (.in(1'b1), .out(transistor_20_out), .gate(1'b1));
  Pull_Resistor pull_resistor_1 (.node(transistor_20_out));
  Pull_Resistor #(.pull(1)) pull_resistor_2 (.node(pull_resistor_2_node));
  Pull_Resistor pull_resistor_3 (.node(transistor_19_out));
  // Probe on transistor_20_out
  Pull_Resistor pull_resistor_4 (.node(pull_resistor_4_node));
  // Probe on pull_resistor_2_node
  // Probe on transistor_19_out
  // Probe on pull_resistor_4_node
endmodule
