// Logisim project 012_FullAdder.circ as structural Verilog: 1 circuit, main circuit main
module main (
);

  wire nand_1_out, nand_2_out, nand_3_out, nand_4_out, nand_5_out, nand_6_out, nand_7_out, nand_8_out,
       nand_9_out, nand_10_out, nand_11_out, nand_12_out, nand_13_out, nand_14_out, nand_15_out, nand_16_out,
       nand_17_out, nand_18_out, nand_19_out, nand_20_out, nand_21_out, nand_22_out;

  nand nand_1 (nand_1_out, 1'b0, 1'b1);
  nand nand_2 (nand_2_out, 1'b1, 1'b1);
  nand nand_3 (nand_3_out, 1'b0, 1'b0);
  nand nand_4 (nand_4_out, 1'b1, 1'b0);
  nand nand_5 (nand_5_out, 1'b0, nand_1_out);
  nand nand_6 (nand_6_out, nand_1_out, 1'b1);
  nand nand_7 (nand_7_out, nand_2_out, nand_3_out);
  nand nand_8 (nand_8_out, nand_5_out, nand_6_out);
  nand nand_9 (nand_9_out, nand_7_out, nand_4_out);
  nand nand_10 (nand_10_out, nand_8_out, 1'b1);
  nand nand_11 (nand_11_out, nand_9_out, nand_9_out);
  nand nand_12 (nand_12_out, nand_8_out, nand_10_out);
  nand nand_13 (nand_13_out, nand_10_out, 1'b1);
  nand nand_14 (nand_14_out, nand_12_out, nand_13_out);
  // Probe on nand_14_out
  // Probe on nand_15_out
  nand nand_15 (nand_15_out, nand_10_out, nand_1_out);
  nand nand_16 (nand_16_out, nand_11_out, nand_11_out);
  nand nand_17 (nand_17_out, 1'b1, 1'b1);
  nand nand_18 (nand_18_out, nand_11_out, 1'b1);
  nand nand_19 (nand_19_out, nand_16_out, nand_17_out);
  nand nand_20 (nand_20_out, nand_19_out, nand_18_out);
  nand nand_21 (nand_21_out, nand_20_out, nand_20_out);
  // Probe on nand_21_out
  nand nand_22 (nand_22_out, nand_18_out, nand_4_out);
  // Probe on nand_22_out
endmodule
