// Logisim project 014_TestFlipFlop.circ as structural Verilog: 1 circuit, main circuit main
module main (
);

  wire clock_1_out, nand_1_out, nand_2_out, nand_3_out, nand_4_out, nand_5_out;

  nand nand_1 (nand_1_out, 1'b0, 1'b0);
  Clock clock_1 (.out(clock_1_out));
  nand nand_2 (nand_2_out, 1'b0, clock_1_out);
  nand nand_3 (nand_3_out, nand_1_out, clock_1_out);
  nand nand_4 (nand_4_out, nand_2_out, nand_5_out);
  nand nand_5 (nand_5_out, nand_4_out, nand_3_out);
  // Probe on nand_4_out
  // Probe on nand_5_out
endmodule
