// Logisim project 017_Counter.circ as structural Verilog: 1 circuit, main circuit main
module main (
);

  wire and_1_out, and_2_out, and_3_out, and_4_out, and_5_out, and_6_out, and_7_out, clock_1_out, d_ff_1_q,
       d_ff_2_q, d_ff_3_q, not_1_out, not_2_out, not_3_out, not_4_out, not_5_out, not_6_out, not_7_out,
       or_1_out, or_2_out, xor_1_out;

  not not_1 (not_1_out, d_ff_1_q);
  not not_2 (not_2_out, d_ff_3_q);
  not not_3 (not_3_out, d_ff_2_q);
  not not_4 (not_4_out, 1'b1);
  not not_5 (not_5_out, d_ff_3_q);
  not not_6 (not_6_out, 1'b1);
  not not_7 (not_7_out, d_ff_2_q);
  and and_1 (and_1_out, not_1_out, d_ff_2_q, d_ff_3_q, 1'b1);
  and and_2 (and_2_out, d_ff_1_q, not_2_out);
  and and_3 (and_3_out, d_ff_1_q, not_3_out);
  and and_4 (and_4_out, d_ff_1_q, not_4_out);
  and and_5 (and_5_out, d_ff_2_q, not_5_out);
  and and_6 (and_6_out, d_ff_2_q, not_6_out);
  and and_7 (and_7_out, d_ff_3_q, 1'b1, not_7_out);
  Clock clock_1 (.out(clock_1_out));
  or or_1 (or_1_out, and_1_out, and_2_out, and_3_out, and_4_out);
  or or_2 (or_2_out, and_5_out, and_6_out, and_7_out);
  xor xor_1 (xor_1_out, d_ff_3_q, 1'b1);
  D_Flip_Flop d_ff_1 (.clk(clock_1_out), .D(or_1_out), .Q(d_ff_1_q));  // open: Qn, preset, en, reset
  D_Flip_Flop d_ff_2 (.clk(clock_1_out), .D(or_2_out), .Q(d_ff_2_q));  // open: Qn, preset, en, reset
  D_Flip_Flop d_ff_3 (.clk(clock_1_out), .D(xor_1_out), .Q(d_ff_3_q));  // open: Qn, preset, en, reset
  // Probe on d_ff_1_q
  // Probe on d_ff_2_q
  // Probe on d_ff_3_q
endmodule
