// Logisim project 104_FlipFlop.circ as structural Verilog: 1 circuit, main circuit main
module main (
);

  wire clock_1_out, clock_2_out, nand_1_out, nand_2_out, nand_3_out, nand_4_out, nand_5_out, nand_6_out,
       nand_7_out, nand_8_out, nand_9_out, nand_10_out, nand_11_out, nand_12_out, nand_13_out, nand_14_out,
       nand_15_out;

  Clock clock_1 (.out(clock_1_out));
  Clock clock_2 (.out(clock_2_out));
  nand nand_1 (nand_1_out, 1'b0, nand_2_out);
  nand nand_2 (nand_2_out, nand_1_out, 1'b1);
  // Probe on nand_1_out
  // Probe on nand_2_out
  nand nand_3 (nand_3_out, 1'b0, clock_1_out);
  nand nand_4 (nand_4_out, nand_3_out, clock_1_out);
  nand nand_5 (nand_5_out, 1'b1, clock_2_out);
  nand nand_6 (nand_6_out, nand_5_out, clock_2_out);
  // Probe on nand_7_out
  nand nand_7 (nand_7_out, nand_3_out, nand_8_out);
  // Probe on nand_8_out
  nand nand_8 (nand_8_out, nand_7_out, nand_4_out);
  nand nand_9 (nand_9_out, nand_5_out, nand_10_out);
  nand nand_10 (nand_10_out, nand_9_out, nand_6_out);
  // Probe on nand_10_out
  nand nand_11 (nand_11_out, clock_2_out, clock_2_out);
  // Probe on nand_9_out
  nand nand_12 (nand_12_out, nand_9_out, nand_11_out);
  nand nand_13 (nand_13_out, nand_12_out, nand_11_out);
  nand nand_14 (nand_14_out, nand_12_out, nand_15_out);
  nand nand_15 (nand_15_out, nand_14_out, nand_13_out);
  // Probe on nand_14_out
  // Probe on nand_15_out

  // Notes on the sheet:
  //   SR Latch
  //   Dtype Latch
  //   Dtype FlipFlop
endmodule
