// Logisim project 106_jk-ff-template-new.circ as structural Verilog: 1 circuit, main circuit main
module main (
);

  wire clock_1_out, multiplexer_1_out, multiplexer_2_out, multiplexer_3_out, multiplexer_4_out, nand_1_out,
       nand_2_out, nand_3_out, nand_4_out, nand_5_out, nand_6_out, nand_7_out, nand_8_out, nand_9_out;

  Clock clock_1 (.out(clock_1_out));
  Multiplexer multiplexer_1 (.in0(nand_9_out), .in1(1'b0), .out(multiplexer_1_out), .sel(1'b0));  // open: en
  Multiplexer multiplexer_2 (.in0(1'b1), .in1(1'b0), .out(multiplexer_2_out), .sel(1'b0));  // open: en
  Multiplexer multiplexer_3 (.in0(1'b1), .in1(1'b1), .out(multiplexer_3_out), .sel(1'b0));  // open: en
  Multiplexer multiplexer_4 (.in0(nand_8_out), .in1(1'b1), .out(multiplexer_4_out), .sel(1'b0));  // open: en
  nand nand_1 (nand_1_out, multiplexer_1_out, clock_1_out, multiplexer_2_out);
  nand nand_2 (nand_2_out, multiplexer_3_out, clock_1_out, multiplexer_4_out);
  nand nand_3 (nand_3_out, nand_1_out, nand_4_out);
  nand nand_4 (nand_4_out, nand_3_out, nand_2_out);
  // Probe on nand_3_out
  // Probe on nand_4_out
  nand nand_5 (nand_5_out, clock_1_out, clock_1_out);
  nand nand_6 (nand_6_out, nand_3_out, nand_5_out);
  nand nand_7 (nand_7_out, nand_5_out, nand_4_out);
  nand nand_8 (nand_8_out, nand_6_out, nand_9_out);
  nand nand_9 (nand_9_out, nand_8_out, nand_7_out);
  // Probe on nand_8_out
  // Probe on nand_9_out

  // Notes on the sheet:
  //   J
  //   Clock
  //   K
  //   Reset'
  //   Feedback X
  //   Feedback Y
endmodule
